// Logisim project Restoring_division.circ as structural Verilog: 1 circuit, main circuit main
// 1x4
module main (
  input  [3:0] N,
  input  [3:0] in_2,
  input  [3:0] in_3,
  input  [3:0] in_4,
  input  [1:0] in_5,
  input  in_6,
  input  in_7,
  input  in_8,
  input  in_9,
  input  in_10,
  input  [3:0] in_11,
  input  [1:0] in_12,
  input  [4:0] Add_1,
  input  [4:0] A,
  output [3:0] Quotient,
  output [4:0] Remainder,
  output [4:0] out_17
);

  wire clock_1_out, clock_2_out, clock_3_out, clock_4_out, comparator_1_eq, comparator_1_gt, comparator_2_gt,
       multiplexer_2_out, multiplexer_4_out, not_1_out, not_2_out, xor_1_out;
  wire [0:0] not_4_out;
  wire [3:0] counter_1_q, counter_2_q, demultiplexer_1_out0, demultiplexer_1_out1, demultiplexer_1_out2,
       demultiplexer_1_out3, multiplexer_1_out, multiplexer_3_out, multiplexer_7_out, ram_1_data,
       register_1_q, register_2_q, register_3_q, register_4_q, register_5_q, register_7_q, register_10_q,
       subtractor_1_out;
  wire [4:0] adder_2_out, not_3_out, register_6_q, register_8_q, register_9_q, register_11_q;
  wire [8:0] multiplexer_5_out, shifter_1_out;

  Multiplexer #(.width(4)) multiplexer_1 (
    .in0(in_11), .in1(multiplexer_7_out), .out(multiplexer_1_out), .sel(in_9));  // open: en
  Clock clock_1 (.out(clock_1_out));
  Clock clock_2 (.out(clock_2_out));
  Clock clock_3 (.out(clock_3_out));
  RAM #(.addrWidth(4), .dataWidth(4), .bus("separate")) ram_1 (
    .addr(in_4), .din(multiplexer_1_out), .data(ram_1_data), .str(in_7), .sel(in_10), .clk(clock_1_out),
    .ld(in_6));  // open: clr
  Counter #(.width(4), .max('h4)) counter_1 (.Q(counter_1_q), .clk(clock_3_out));  // open: load, D, count, carry, clr
  Register #(.width(4)) register_1 (.D(ram_1_data), .Q(register_1_q), .clk(clock_1_out));  // open: en, clr
  Demultiplexer #(.select(2), .width(4)) demultiplexer_1 (
    .out0(demultiplexer_1_out0), .out1(demultiplexer_1_out1), .out2(demultiplexer_1_out2),
    .out3(demultiplexer_1_out3), .in(register_1_q), .sel(in_5));  // open: en
  Register #(.width(4)) register_2 (.D(demultiplexer_1_out3), .Q(register_2_q), .clk(clock_2_out));  // open: en, clr
  Register #(.width(4)) register_3 (.D(demultiplexer_1_out2), .Q(register_3_q), .clk(clock_2_out));  // open: en, clr
  Register #(.width(4)) register_4 (.D(demultiplexer_1_out1), .Q(register_4_q), .clk(clock_2_out));  // open: en, clr
  Register #(.width(4)) register_5 (.D(demultiplexer_1_out0), .Q(register_5_q), .clk(clock_2_out));  // open: en, clr
  Subtractor #(.width(4)) subtractor_1 (.a(N), .b(counter_1_q), .out(subtractor_1_out), .bin(1'b0));  // open: bout
  Comparator #(.width(4)) comparator_1 (
    .a(subtractor_1_out), .b(in_2), .gt(comparator_1_gt), .eq(comparator_1_eq));  // open: lt
  not not_1 (not_1_out, xor_1_out);
  Multiplexer multiplexer_2 (.in0(1'b0), .in1(clock_3_out), .out(multiplexer_2_out), .sel(not_1_out));  // open: en
  Multiplexer #(.select(2), .width(4)) multiplexer_3 (
    .in0(register_2_q), .in1(register_3_q), .in2(register_4_q), .in3(register_5_q), .out(multiplexer_3_out),
    .sel(in_12));  // open: en
  Multiplexer multiplexer_4 (.in0(1'b0), .in1(clock_3_out), .out(multiplexer_4_out), .sel(xor_1_out));  // open: en
  Register #(.width(5)) register_6 (
    .D({1'b0, multiplexer_3_out}), .Q(register_6_q), .clk(clock_4_out));  // open: en, clr
  Clock clock_4 (.out(clock_4_out));
  xor xor_1 (xor_1_out, comparator_1_gt, comparator_1_eq);
  not not_2 (not_2_out, xor_1_out);
  Register #(.width(4)) register_7 (
    .D(register_1_q), .en(not_2_out), .Q(register_7_q), .clk(multiplexer_2_out));  // open: clr
  Register #(.width(5)) register_8 (
    .D(register_6_q), .en(not_2_out), .Q(register_8_q), .clk(multiplexer_2_out));  // open: clr
  Register #(.width(5)) register_9 (.D(A), .en(not_2_out), .Q(register_9_q), .clk(multiplexer_2_out));  // open: clr
  Counter #(.width(4), .max('h3)) counter_2 (
    .Q(counter_2_q), .clk(multiplexer_4_out));  // open: load, D, count, carry, clr
  assign not_3_out = ~register_8_q;  // NOT_Gate not_3, 5 bits wide
  Comparator #(.width(4)) comparator_2 (.a(counter_2_q), .b(in_3), .gt(comparator_2_gt));  // open: eq, lt
  Multiplexer #(.width(9)) multiplexer_5 (
    .in0({register_9_q, register_7_q}), .in1({Remainder, Quotient}), .out(multiplexer_5_out),
    .sel(comparator_2_gt));  // open: en
  Adder #(.width(5)) adder_1 (.a(not_3_out), .b(Add_1), .out(out_17));  // open: cin, cout
  Shifter #(.width(9)) shifter_1 (.in(multiplexer_5_out), .\dist (4'b0001), .out(shifter_1_out));
  Register #(.width(4)) register_10 (
    .D(shifter_1_out[3:0]), .en(xor_1_out), .Q(register_10_q), .clk(multiplexer_4_out));  // open: clr
  Register #(.width(5)) register_11 (
    .D(shifter_1_out[8:4]), .en(xor_1_out), .Q(register_11_q), .clk(multiplexer_4_out));  // open: clr
  not not_4 (not_4_out[0], adder_2_out[4]);
  Adder #(.width(5)) adder_2 (.a(register_11_q), .b(out_17), .out(adder_2_out));  // open: cin, cout
  Multiplexer #(.width(5)) multiplexer_6 (
    .in0(adder_2_out), .in1(register_11_q), .out(Remainder), .sel(adder_2_out[4]));  // open: en
  Adder #(.width(4)) adder_3 (.a(register_10_q), .b({3'b000, not_4_out[0]}), .out(Quotient));  // open: cin, cout
  Multiplexer #(.width(4)) multiplexer_7 (
    .in0(Quotient), .in1(Remainder[3:0]), .out(multiplexer_7_out), .sel(in_8));  // open: en

  // Notes on the sheet:
  //   Main Memory
  //   Clock
  //   Processor Register File
  //   Q Obtained from Memory
  //   Q
  //   M
  //   A
  //   Shift AQ
  //   M-2's Compliment
  //   Temp Registers
  //   A=A-M
  //   LOOP
  //   Restore A
endmodule
